# Fritzing sketch dataLogger (saved by Fritzing 0.9.3b)

parts:
  WeMos_D1_Mini1 = WeMos D1 Mini
  WeMos_D1_Mini_OLED_Shield1 = WeMos D1 Mini OLED Shield
  DHT2 = DHT11 Humitidy and Temperature Sensor  # not connected

nets:
  N1: WeMos_D1_Mini1.D1, WeMos_D1_Mini_OLED_Shield1.D1
  N2: WeMos_D1_Mini1.D2, WeMos_D1_Mini_OLED_Shield1.D2

notes:
  GMF AeroAsia
  Data Logger
  Temporary Store - Line 7
  DHT11 - one wire comm.
  OLED - I2C

custom parts:
  DHT11 Humitidy and Temperature Sensor: DHT11 Humidity and Temperature Sensor
